# Fritzing sketch ElectricScrewdriverSchematic (saved by Fritzing 0.9.3b)
breadboards: 1

parts:
  U2 = LIPO-110mAh [package=lipo-110]
  Part1 = Power Cell LiPo Charger/Booster
  M1 = DC Motor
  S1 = Pushbutton [package="[SMD]"]
  S2 = Pushbutton [package="[SMD]"]
  R1 = Resistor [tolerance=±5% resistance=220 package="2010 [SMD]"]
  R2 = Resistor [tolerance=±5% resistance=220 package="2010 [SMD]"]
  Part3 = Adafruit DRV8833 DC/Stepper Motor Driver [part_number="Adafruit #3297"]

nets:
  N1: U2.+, Part1.VCC
  GND: U2.-, Part1.GND, R1.Pin_1, R2.Pin_1, Part3.GND
  N2: Part1.5VIN, S1.Pin_3, S1.Pin_4, S2.Pin_3, S2.Pin_4, Part3.VMOTOR
  N3: M1.pin_1, Part3.AOUT2
  N4: M1.pin_2, Part3.AOUT1
  N5: S1.Pin_1, S1.Pin_2, R1.Pin_0, Part3.AIN1
  N6: S2.Pin_1, S2.Pin_2, R2.Pin_0, Part3.AIN2

custom parts:
  Adafruit DRV8833 DC/Stepper Motor Driver: Spin two DC motors or step one bi-polar or uni-polar stepper with up to 1.2A per channel using the DRV8833. This motor driver chip is a nice alternative to the TB6612 driver. Like that chip, you get 2 full H-bridges, but this chip is better for low voltage uses (can run from 2.7V up to 10.8V motor power) and has built in current limiting capability. We set it up for 1A current limiting so you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
